# Fritzing sketch StanBase (saved by Fritzing 0.9.6b)

parts:
  17HS4401_Right_Stepper_Motor = Stepper Motor - Bipolar
  17HS4401_Left_Stepper_Motor = Stepper Motor - Bipolar
  Arduino_Nano = Arduino Nano (Rev3.0)
  A4988_Board = Pololu A4988 [package=SO16]
  A4988_Board_2 = Pololu A4988 [package=SO16]
  J3 = XT60 Connector [package=THT]
  NeoMatrix_8x8 = NeoPixel NeoMatrix 8x8 [part_number=1487]
  TowerPro_MG90S_Tilt_Servo = Basic Servo
  TowerPro_MG90S_Pan_Servo = Basic Servo
  Gyro_Breakout_Board = Single Axis Gyro
  Accelerometer_Breakout_Board = ADXL345 Breakout Board
  S1 = Taiway 100-SP-X-T1 SPDT Miniature Toggle Switch [part_number=100-SP-X-T1-0-0-B1-M1 package=THT]
  DC/DC_Converter = Mini-360 DC-DC Buck converter [package=THT]
  R1 = Resistor [tolerance=±5% resistance=62k power=0.25 package=THT]
  R2 = Resistor [tolerance=±5% resistance=100k power=0.25 package=THT]
  R3 = Resistor [tolerance=±5% resistance=470 power=0.25 package=THT]
  C3 = Electrolytic Capacitor [capacitance=100µF voltage=50V package="200 mil [THT, electrolytic]"]
  C4 = Electrolytic Capacitor [capacitance=100µF voltage=50V package="200 mil [THT, electrolytic]"]
  C5 = Electrolytic Capacitor [capacitance=10µF voltage=35V package="200 mil [THT, electrolytic]"]

nets:
  N1: 17HS4401_Right_Stepper_Motor.A, A4988_Board_2.1A
  N2: 17HS4401_Right_Stepper_Motor.C, A4988_Board_2.1B
  N3: 17HS4401_Right_Stepper_Motor.B, A4988_Board_2.2A
  N4: 17HS4401_Right_Stepper_Motor.D, A4988_Board_2.2B
  N5: 17HS4401_Left_Stepper_Motor.A, A4988_Board.1A
  N6: 17HS4401_Left_Stepper_Motor.C, A4988_Board.1B
  N7: 17HS4401_Left_Stepper_Motor.B, A4988_Board.2A
  N8: 17HS4401_Left_Stepper_Motor.D, A4988_Board.2B
  GND: Arduino_Nano.GND, A4988_Board.GND#8, A4988_Board_2.GND#8, NeoMatrix_8x8.GND, TowerPro_MG90S_Tilt_Servo.gnd, TowerPro_MG90S_Pan_Servo.gnd, Gyro_Breakout_Board.GND1, Accelerometer_Breakout_Board.GND2, DC/DC_Converter.OUT-, C5.-
  N9: Arduino_Nano.D2, Accelerometer_Breakout_Board.I1
  N10: Arduino_Nano.D3, TowerPro_MG90S_Tilt_Servo.pulse
  N11: Arduino_Nano.D4, A4988_Board.MS1, A4988_Board_2.MS1
  N12: Arduino_Nano.D5, A4988_Board.DIR
  N13: Arduino_Nano.D6, A4988_Board.MS2, A4988_Board_2.MS2
  N14: Arduino_Nano.D7, A4988_Board_2.DIR
  N15: Arduino_Nano.D8, A4988_Board.SLEEP, A4988_Board_2.SLEEP
  N16: Arduino_Nano.D9, A4988_Board.STEP
  N17: Arduino_Nano.D10, A4988_Board_2.STEP
  N18: Arduino_Nano.D11/MOSI, TowerPro_MG90S_Pan_Servo.pulse
  N19: Arduino_Nano.D12/MISO, R3.Pin_0
  N20: Arduino_Nano.5V, Gyro_Breakout_Board.5V1, Accelerometer_Breakout_Board.5V2
  N21: Arduino_Nano.A7, Gyro_Breakout_Board.Rate
  N22: Arduino_Nano.A6, R1.Pin_0, R2.Pin_1
  N23: Arduino_Nano.A5, Accelerometer_Breakout_Board.SCL
  N24: Arduino_Nano.A4, Accelerometer_Breakout_Board.SDA
  VDD: A4988_Board.RESET, A4988_Board.VDD, A4988_Board_2.RESET, A4988_Board_2.VDD, NeoMatrix_8x8.VDD, TowerPro_MG90S_Tilt_Servo.vcc, TowerPro_MG90S_Pan_Servo.vcc, DC/DC_Converter.OUT+, C5.+
  N25: A4988_Board.GND#14, A4988_Board_2.GND#14, J3.GND, DC/DC_Converter.IN-, R1.Pin_1, C3.-, C4.-
  N26: A4988_Board.VMOT, A4988_Board_2.VMOT, S1.COM, DC/DC_Converter.IN+, R2.Pin_0, C3.+, C4.+
  N27: J3.VCC, S1.L2
  N28: NeoMatrix_8x8.IN, R3.Pin_1

notes:
  stan
  © 2021 David Beaudette

custom parts:
  XT60 Connector: Yellow XT60 connector for high current loads up to 40A
  NeoPixel NeoMatrix 8x8: Put on your sunglasses before wiring up this LED matrix - 64 eye-blistering RGB LEDs adorn the NeoMatrix for a blast of configurable color. Arranged in an 8x8 matrix, each pixel is individually addressable. Only one microcontroller pin is required to control all the LEDs, and you get 24 bit color for each LED.
  Single Axis Gyro: Breakout board for the ADW22307 1-axis analog gyroscope.
  ADXL345 Breakout Board: Breakout board for the ADXL345 accelerometer
  Mini-360 DC-DC Buck converter: Mini-360 DC-DC Buck converter. Tiny buck step down voltage converter, input voltage 4.75 to 23V output 1 to 17V adjustable. Available from ebay and the like.
