# Fritzing sketch StanBase (saved by Fritzing 0.9.3b)

parts:
  17HS4401_Right_Stepper_Motor = Stepper Motor - Bipolar  # not connected
  17HS4401_Left_Stepper_Motor = Stepper Motor - Bipolar  # not connected
  Part1 = Arduino Nano (Rev3.0)  # not connected
  A4988_Board_(Left_Motor) = Pololu A4988 [package=SO16]
  A4988_Board_(Right_Motor) = Pololu A4988 [package=SO16]
  J3 = XT60 Connector [package=THT]
  Part3 = NeoPixel NeoMatrix 8x8 [part_number=1487]
  MEZD71202A-G_or_P7805-2000-S = Voltage Regulator [package=to220-igo]
  TowerPro_MG90S_Tilt_Servo = Basic Servo
  TowerPro_MG90S_Pan_Servo = Basic Servo

nets:
  GND: A4988_Board_(Left_Motor).GND, A4988_Board_(Right_Motor).GND, J3.GND, MEZD71202A-G_or_P7805-2000-S.GND, TowerPro_MG90S_Tilt_Servo.gnd, TowerPro_MG90S_Pan_Servo.gnd
  N1: A4988_Board_(Left_Motor).VMOT, A4988_Board_(Right_Motor).VMOT, J3.VCC, MEZD71202A-G_or_P7805-2000-S.IN
  VCC: Part3.VDD, MEZD71202A-G_or_P7805-2000-S.OUT, TowerPro_MG90S_Tilt_Servo.vcc, TowerPro_MG90S_Pan_Servo.vcc

notes:
  2A max.

custom parts:
  XT60 Connector: Yellow XT60 connector for high current loads up to 40A
  NeoPixel NeoMatrix 8x8: Put on your sunglasses before wiring up this LED matrix - 64 eye-blistering RGB LEDs adorn the NeoMatrix for a blast of configurable color. Arranged in an 8x8 matrix, each pixel is individually addressable. Only one microcontroller pin is required to control all the LEDs, and you get 24 bit color for each LED.
